# Fritzing sketch L-Star (saved by Fritzing 0.9.1b)
breadboards: 1

parts:
  Propeller1 = Parallax Propeller D40 [package="DIP [THT]"]
  IC1 = WDC 65C02S [chip_label="WDC 65C02" package="DIP (Dual Inline) [THT]"]
  IC2 = 24LC256 [package=THT]
  RESET_PROP = Pushbutton [package="[THT]"]
  RESET_65C02 = Pushbutton [package="[THT]"]
  R1 = Resistor [tolerance=±5% resistance=3.3k package=THT]
  R2 = Resistor [tolerance=±5% resistance=3.3k package=THT]
  5MHz = CRYSTAL [package=hc49us]
  U1 = mini DIN 6 Connector [package=mini-din6]
  JP1 = RCA [package=rca_lock]
  R3 = Resistor [tolerance=±5% resistance=220 package=THT]
  IC3 = Voltage Regulator [package=TO220]
  J1 = Power Jack [package=power_jack_pth_lock]
  R4 = Resistor [tolerance=±5% resistance=100 package=THT]
  R5 = Resistor [tolerance=±5% resistance=100 package=THT]
  R6 = Resistor [tolerance=±5% resistance=10k package=THT]
  R7 = Resistor [tolerance=±5% resistance=10k package=THT]
  IC4 = Voltage Regulator [package=78xxl]

nets:
  N1: Propeller1.P0, IC1.D0
  N2: Propeller1.P1, IC1.D1
  N3: Propeller1.P2, IC1.D2
  N4: Propeller1.P3, IC1.D3
  N5: Propeller1.P4, IC1.D4
  N6: Propeller1.P5, IC1.D5
  N7: Propeller1.P6, IC1.D6
  N8: Propeller1.P7, IC1.D7
  GND: Propeller1.VSS, Propeller1.BOEn, IC1.VSS, IC2.A0, IC2.A1, IC2.A2, IC2.0V, IC2.WP_-_Write_Protect, RESET_PROP.Pin_1, RESET_PROP.Pin_2, RESET_65C02.Pin_3, RESET_65C02.Pin_4, U1.3, JP1.SHELL, IC3.GND, J1.GND, IC4.GND
  N9: Propeller1.RESn, RESET_PROP.Pin_3, RESET_PROP.Pin_4
  VDD: Propeller1.VDD, IC1.VDD, IC2.+V, R1.Pin_0, R2.Pin_1, IC3.OUT, R6.Pin_1, R7.Pin_1
  N10: Propeller1.P8, IC1.A0
  N11: Propeller1.P9, IC1.A1
  N12: Propeller1.P10, IC1.A2
  N13: Propeller1.P11, IC1.A3
  N14: Propeller1.P12, IC1.A4
  N15: Propeller1.P13, IC1.A5
  N16: Propeller1.P14, IC1.A6
  N17: Propeller1.P15, IC1.A7
  N18: Propeller1.P16, IC1.A8
  N19: Propeller1.P17, IC1.A9
  N20: Propeller1.P18, IC1.A10
  N21: Propeller1.P19, IC1.A11
  N22: Propeller1.P20, IC1.A12
  N23: Propeller1.P21, IC1.A13
  N24: Propeller1.P22, IC1.A14
  N25: Propeller1.P23, IC1.A15
  N26: Propeller1.XI, 5MHz.2
  N27: Propeller1.XO, 5MHz.1
  N28: Propeller1.P24, IC1.RWB
  N29: Propeller1.P25, R3.Pin_1
  N30: Propeller1.P26, R4.Pin_1
  N31: Propeller1.P27, R5.Pin_1
  N32: Propeller1.P28, IC1.PHI2, IC2.SCL_-_I2C_Clock
  N33: Propeller1.P29, IC2.SDA_-_I2C_Data
  N34: IC1.RDY, IC1.IRQB, IC1.NMIB, IC1.BE, IC1.SOB, R2.Pin_0
  N35: IC1.RESB, RESET_65C02.Pin_1, RESET_65C02.Pin_2, R1.Pin_1
  N36: U1.1, R4.Pin_0, R6.Pin_0
  N37: U1.4, IC3.IN, IC4.OUT
  N38: U1.5, R5.Pin_0, R7.Pin_0
  N39: JP1.PIN, R3.Pin_0
  N40: J1.PWR, IC4.IN

custom parts:
  WDC 65C02S: The Western Design Center version of the 65C02
  Voltage Regulator: Voltage Regulator Standard voltage regulator. IGO (Input Ground Output).
